// Logisim project sagui.circ as structural Verilog: 4 circuits, main circuit main
module main (
);

  wire clk, cls;
  wire [7:0] bancoregs_1_saidaa, bancoregs_1_saidab, rom_1_data, ula_1_saida;
  wire [23:0] adder_1_out, register_1_q;

  Adder #(.width(24)) adder_1 (.a(register_1_q), .b(24'h1), .out(adder_1_out), .cin(1'b0));  // open: cout
  Register #(.width(24)) register_1 (.D(adder_1_out), .en(1'b1), .clk(clk), .Q(register_1_q), .clr(cls));
  ROM #(.addrWidth(24)) rom_1 (.addr(register_1_q), .data(rom_1_data));
  Clock clock_1 (.out(clk));
  Button button_1 (.out(cls));
  MemControle memcontrole_1 (.Entrada(rom_1_data[7:4]));
  bancoRegs bancoregs_1 (
    .saidaA(bancoregs_1_saidaa), .saidaB(bancoregs_1_saidab), .clk(clk), .rst(cls), .ra(rom_1_data[1:0]),
    .rb(rom_1_data[3:2]));  // open: write, dadosEscrita
  ULA ula_1 (.saida(ula_1_saida), .A(bancoregs_1_saidaa), .B(bancoregs_1_saidab));  // open: Op
endmodule

module MemControle (
  input  [3:0] Entrada
);

  ROM #(.addrWidth(4)) rom_1 (.addr(Entrada));  // open: data
endmodule

module ULA (
  input  [7:0] A,
  input  [2:0] Op,
  input  [7:0] B,
  output [7:0] saida
);

  wire or_1_out;
  wire [7:0] adder_1_out, adder_2_out, and_1_out, multiplexer_1_out, multiplexer_2_out, not_1_out, or_2_out,
       shifter_1_out, shifter_2_out;

  or or_1 (or_1_out, B[7], B[6], B[5], B[4], B[3]);
  Adder adder_1 (.a(A), .b(B), .out(adder_1_out), .cin(1'b0));  // open: cout
  Adder adder_2 (.a(A), .b(not_1_out), .out(adder_2_out), .cin(1'b1));  // open: cout
  assign and_1_out = A & B;  // AND_Gate and_1, 8 bits wide
  assign or_2_out = A | B;  // OR_Gate or_2, 8 bits wide
  assign not_1_out = ~B;  // NOT_Gate not_1, 8 bits wide
  Shifter shifter_1 (.in(A), .\dist (B[2:0]), .out(shifter_1_out));
  Shifter #(.shift("lr")) shifter_2 (.in(A), .\dist (B[2:0]), .out(shifter_2_out));
  Multiplexer #(.width(8)) multiplexer_1 (
    .in0(shifter_1_out), .in1({8{1'b0}}), .out(multiplexer_1_out), .sel(or_1_out));
  Multiplexer #(.width(8)) multiplexer_2 (
    .in0(shifter_2_out), .in1({8{1'b0}}), .out(multiplexer_2_out), .sel(or_1_out));
  Multiplexer #(.select(3), .width(8)) multiplexer_3 (
    .in0(adder_1_out), .in1(adder_2_out), .in2(and_1_out), .in3(or_2_out), .in4(not_1_out),
    .in5(multiplexer_1_out), .in6(multiplexer_2_out), .in7(B), .out(saida), .sel(Op));
endmodule

module bancoRegs (
  input  [7:0] dadosEscrita,
  input  write,
  input  clk,
  input  rst,
  input  [1:0] ra,
  input  [1:0] rb,
  output [7:0] saidaA,
  output [7:0] saidaB
);

  wire [7:0] demultiplexer_1_out0, demultiplexer_1_out1, demultiplexer_1_out2, demultiplexer_1_out3,
       register_1_q, register_2_q, register_3_q;

  Register register_1 (.D(demultiplexer_1_out1), .en(write), .clk(clk), .Q(register_1_q), .clr(rst));
  Multiplexer #(.select(2), .width(8)) multiplexer_1 (
    .in0({8{1'b0}}), .in1(register_1_q), .in2(register_2_q), .in3(register_3_q), .out(saidaA), .sel(ra));
  Multiplexer #(.select(2), .width(8)) multiplexer_2 (
    .in0({8{1'b0}}), .in1(register_1_q), .in2(register_2_q), .in3(register_3_q), .out(saidaB), .sel(rb));
  Demultiplexer #(.select(2), .width(8)) demultiplexer_1 (
    .out0(demultiplexer_1_out0), .out1(demultiplexer_1_out1), .out2(demultiplexer_1_out2),
    .out3(demultiplexer_1_out3), .in(dadosEscrita), .sel(ra));
  Register register_2 (.D(demultiplexer_1_out2), .en(write), .clk(clk), .Q(register_2_q), .clr(rst));
  Register register_3 (.D(demultiplexer_1_out3), .en(write), .clk(clk), .Q(register_3_q), .clr(rst));
  // also tied to GND on the sheet: {demultiplexer_1_out0[0], demultiplexer_1_out0[1], demultiplexer_1_out0[2], demultiplexer_1_out0[3], demultiplexer_1_out0[4], demultiplexer_1_out0[5], demultiplexer_1_out0[6], demultiplexer_1_out0[7]}
endmodule
